# Fritzing sketch fritzing board (saved by Fritzing 0.9.5d)
breadboards: 2

parts:
  A1 = ESP32 DevKitc V4
  OLED1 = OLED 128x64 I2C Monochrome Display
  OMRON1 = OMRON PCB Power Relay – G5LE [part_number="G5LE-1\r\n" package=THT]
  D1 = Zener Diode [part_number=1N4732A breakdown_voltage=3.6V package="300 mil [THT]"]
  U1 = DIODE-ZENER [package=diode-zener]  # not connected
  Q1 = NPN-Transistor [package="TO92 [THT]"]
  R1 = Resistor [tolerance=±5% resistance=220 package=THT]
  S1 = Round Pushbutton
  R2 = Resistor [tolerance=±5% resistance=1k package=THT]
  LED1 = LED - 3mm [color="Green (555nm)" package="3 mm [THT]"]
  R3 = Resistor [tolerance=±5% resistance=220 package=THT]

nets:
  N1: A1.Pin_30, R1.Pin_1
  N2: A1.Pin_32, A1.Pin_38
  N3: OLED1.GND, OMRON1.COIL1, Q1.C, R2.Pin_0
  N4: OLED1.VDD, OMRON1.C, D1.cathode, R3.Pin_1
  N5: OMRON1.COIL2, D1.anode, Q1.E
  N6: OMRON1.B, LED1.anode
  N7: Q1.B, R1.Pin_0
  N8: S1.leg0, R2.Pin_1
  N9: LED1.cathode, R3.Pin_0

custom parts:
  ESP32 DevKitc V4: ESP32-DevKitC board with ESP32-WROOM-32 module. ESP32-DevKitC V4 is a small-sized ESP32-based development board produced by Espressif. Most of the pins on the ESP module are broken out to the pin headers on the board. The pins D0, D1, D2, D3, CMD and CLK are used internally for communication between ESP32 and SPI flash memory. They are grouped on both sides near the USB connector. Avoid using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

// code stored in the sketch: Untitled.bas

